# Fritzing sketch البصمة (saved by Fritzing 0.9.3b)
circuit board: 20.1068cm x 10.9226cm

parts:
  Part1 = sensor_biometrico
  اردوينو = Arduino Uno (Rev3)

nets:
  VCC: Part1.VCC, اردوينو.5V
  N1: Part1.TX, اردوينو.D2
  N2: Part1.RX, اردوينو.D3_PWM
  GND: Part1.GND, اردوينو.GND

notes:
  البصمة

custom parts:
  sensor_biometrico: Adafruit Optical Fingerprint Sensor
