# Fritzing sketch قارى البطاقات (saved by Fritzing 0.9.3b)
circuit board: 14.4417cm x 12.2467cm
breadboards: 1

parts:
  Part2 = RFID-RC522-v2
  Part1 = Arduino Uno (Rev3) - ICSP

nets:
  N1: Part2.SDA, Part1.D10_PWM/SS
  N2: Part2.SCK, Part1.D13/SCK
  N3: Part2.MOSI, Part1.D11_PWM/MOSI
  N4: Part2.MISO, Part1.D12/MISO
  GND: Part2.GND, Part1.GND
  N5: Part2.RST, Part1.D9_PWM
  N6: Part2.3_3V, Part1.3V3

custom parts:
  RFID-RC522-v2: A simple China made RFID-RC522 Reader; do check the pin labels, as this is a MFRC522 based clone.
